# Fritzing sketch Untitled Sketch (saved by Fritzing 0.9.3b)
breadboards: 1

parts:
  U1 = ESP32-38PinWide [part_number=ESP32-38PinWide]  # not connected
  M1 = DFRobot HCHO sensor [package=THT]
  ZS-042_RTC1 = ZS-042 RTC Module
  Grove1 = Grove OLED 128x96
  VCC1 = Battery  # not connected

nets:
  VCC: M1.pin2, M1.pin3, ZS-042_RTC1.VCC, Grove1.VCC
  GND: ZS-042_RTC1.GND, ZS-042_RTC1.SDA, ZS-042_RTC1.SCL, Grove1.GND, Grove1.SDA, Grove1.SCL

custom parts:
  ESP32-38PinWide: Generic 38-Pin ESP32 with wide format (only access to one side of pins on a breadboard) based on Stephen Lilley's HiLetgo ESP-WROOM-32 ESP32 ESP-32S Development Board.
  DFRobot HCHO sensor: DFRobot HCHO sensor.
